// Logisim project Ampel.circ as structural Verilog: 7 circuits, main circuit Komplette Schaltung
module Komplette_Schaltung (
);

  wire and_1_out, auto_gelb_1_autogelb, \auto_grün_1_autogrün , auto_rot_1_auto_rot, button_1_out,
       clock_1_out, freigabe_1_freigabe, \fußgänger_grün_1_fußgrün , \fußgänger_rot_1_fußrot ;
  wire [2:0] not_1_out;
  wire [4:0] counter_2_q;
  wire [8:0] counter_1_q;

  Clock clock_1 (.out(clock_1_out));
  Counter #(.width(9), .max('h1ff)) counter_1 (
    .count(1'b1), .Q(counter_1_q), .clk(clock_1_out));  // open: load, D, carry, clr
  Freigabe freigabe_1 (
    .\FußgängerRot (\fußgänger_rot_1_fußrot ), .Knopfdruck(button_1_out),
    .\Autoampel_Grün (\auto_grün_1_autogrün ), .Freigabe(freigabe_1_freigabe));
  and and_1 (and_1_out, counter_1_q[0], counter_1_q[1], counter_1_q[2], counter_1_q[3], counter_1_q[4], counter_1_q[5], counter_1_q[6], counter_1_q[7], counter_1_q[8]);
  Counter #(.width(5), .max('h1f)) counter_2 (
    .load(freigabe_1_freigabe), .D({2'b11, not_1_out[2], 1'b1, not_1_out[0]}), .count(and_1_out),
    .Q(counter_2_q), .clk(clock_1_out));  // open: carry, clr
  not not_1 (not_1_out[0], 1'b1);
  not not_2 (not_1_out[2], 1'b1);
  Auto_Rot auto_rot_1 (
    .Vier(counter_2_q[4]), .Drei(counter_2_q[3]), .Zwei(counter_2_q[2]), .Eins(counter_2_q[1]),
    .Null(counter_2_q[0]), .Auto_Rot(auto_rot_1_auto_rot));
  Auto_Gelb auto_gelb_1 (
    .Vier(counter_2_q[4]), .Drei(counter_2_q[3]), .Zwei(counter_2_q[2]), .Eins(counter_2_q[1]),
    .Null(counter_2_q[0]), .AutoGelb(auto_gelb_1_autogelb));
  \Auto_Grün  \auto_grün_1  (
    .Null(counter_2_q[0]), .Eins(counter_2_q[1]), .Zwei(counter_2_q[2]), .Drei(counter_2_q[3]),
    .Vier(counter_2_q[4]), .\AutoGrün (\auto_grün_1_autogrün ));
  LED led_1 (.in(auto_rot_1_auto_rot));
  LED led_2 (.in(auto_gelb_1_autogelb));
  LED led_3 (.in(\auto_grün_1_autogrün ));
  \Fußgänger_Rot  \fußgänger_rot_1  (
    .Null(counter_2_q[0]), .Eins(counter_2_q[1]), .Zwei(counter_2_q[2]), .Drei(counter_2_q[3]),
    .Vier(counter_2_q[4]), .\FußRot (\fußgänger_rot_1_fußrot ));
  \Fußgänger_Grün  \fußgänger_grün_1  (
    .Null(counter_2_q[0]), .Eins(counter_2_q[1]), .Zwei(counter_2_q[2]), .Drei(counter_2_q[3]),
    .Vier(counter_2_q[4]), .\FußGrün (\fußgänger_grün_1_fußgrün ));
  LED led_4 (.in(\fußgänger_grün_1_fußgrün ));
  LED led_5 (.in(\fußgänger_rot_1_fußrot ));
  Button button_1 (.out(button_1_out));

  // Notes on the sheet:
  //   ZÄHLER 1
  //   FREIGABE
  //   ZÄHLER 2
  //   RESET ZU SEC 26
  //   ROT
  //   GRÜN
  //   ROT FÜR FUßGÄNGER
  //   GELB
  //   GRÜN FÜR FUßGÄNGER
  //   Auto Ampel
  //   GRÜN
  //   ROT
  //   Schalter Fußgänger
  //   Fußgänger Ampel
endmodule

module Auto_Rot (
  input  Vier,
  input  Drei,
  input  Zwei,
  input  Eins,
  input  Null,
  output Auto_Rot
);

  wire _0_out, _1_out, _2_out, _3_out, _4_out, _5_out, _6_out, _7_out, _8_out, _9_out, _10_out, _11_out,
       _30_out, _31_out, not_1_out, not_2_out, not_3_out, not_4_out, not_5_out, not_6_out, not_7_out,
       not_8_out, not_9_out, not_10_out, not_11_out, not_12_out, not_13_out, not_14_out, not_15_out,
       not_16_out, not_17_out, not_18_out, not_19_out, not_20_out, not_21_out, not_22_out, not_23_out,
       not_24_out, not_25_out, not_26_out, not_27_out, not_28_out, not_29_out, not_30_out, not_31_out,
       not_32_out, not_33_out, not_34_out, not_35_out, not_36_out, not_37_out, not_38_out, not_39_out,
       not_40_out, not_41_out;

  not not_1 (not_1_out, Null);
  not not_2 (not_2_out, Eins);
  and _0 (_0_out, not_1_out, not_2_out, not_3_out, not_4_out, not_5_out);
  not not_3 (not_3_out, Zwei);
  not not_4 (not_4_out, Drei);
  not not_5 (not_5_out, Vier);
  not not_6 (not_6_out, Eins);
  not not_7 (not_7_out, Zwei);
  and _1 (_1_out, Null, not_6_out, not_7_out, not_8_out, not_9_out);
  not not_8 (not_8_out, Drei);
  not not_9 (not_9_out, Vier);
  not not_10 (not_10_out, Null);
  and _2 (_2_out, not_10_out, Eins, not_11_out, not_12_out, not_13_out);
  not not_11 (not_11_out, Zwei);
  not not_12 (not_12_out, Drei);
  not not_13 (not_13_out, Vier);
  and _3 (_3_out, Null, Eins, not_14_out, not_15_out, not_16_out);
  not not_14 (not_14_out, Zwei);
  not not_15 (not_15_out, Drei);
  not not_16 (not_16_out, Vier);
  not not_17 (not_17_out, Null);
  not not_18 (not_18_out, Eins);
  and _4 (_4_out, not_17_out, not_18_out, Zwei, not_19_out, not_20_out);
  not not_19 (not_19_out, Drei);
  not not_20 (not_20_out, Vier);
  not not_21 (not_21_out, Eins);
  and _5 (_5_out, Null, not_21_out, Zwei, not_22_out, not_23_out);
  not not_22 (not_22_out, Drei);
  not not_23 (not_23_out, Vier);
  not not_24 (not_24_out, Null);
  and _6 (_6_out, not_24_out, Eins, Zwei, not_25_out, not_26_out);
  not not_25 (not_25_out, Drei);
  not not_26 (not_26_out, Vier);
  and _7 (_7_out, Null, Eins, Zwei, not_27_out, not_28_out);
  not not_27 (not_27_out, Drei);
  not not_28 (not_28_out, Vier);
  not not_29 (not_29_out, Null);
  not not_30 (not_30_out, Eins);
  not not_31 (not_31_out, Zwei);
  and _8 (_8_out, not_29_out, not_30_out, not_31_out, Drei, not_32_out);
  not not_32 (not_32_out, Vier);
  not not_33 (not_33_out, Eins);
  not not_34 (not_34_out, Zwei);
  and _9 (_9_out, Null, not_33_out, not_34_out, Drei, not_35_out);
  not not_35 (not_35_out, Vier);
  not not_36 (not_36_out, Null);
  and _10 (_10_out, not_36_out, Eins, not_37_out, Drei, not_38_out);
  not not_37 (not_37_out, Zwei);
  not not_38 (not_38_out, Vier);
  not not_39 (not_39_out, Zwei);
  and _11 (_11_out, Null, Eins, not_39_out, Drei, not_40_out);
  not not_40 (not_40_out, Vier);
  not not_41 (not_41_out, Null);
  and _30 (_30_out, not_41_out, Eins, Zwei, Drei, Vier);
  and _31 (_31_out, Null, Eins, Zwei, Drei, Vier);
  or or_1 (Auto_Rot, _0_out, _1_out, _2_out, _3_out, _4_out, _5_out, _6_out, _7_out, _8_out, _9_out, _10_out, _11_out, _30_out, _31_out);
endmodule

module Auto_Gelb (
  input  Vier,
  input  Drei,
  input  Zwei,
  input  Eins,
  input  Null,
  output AutoGelb
);

  wire _11_out, _29_out, not_1_out, not_2_out, not_3_out;

  not not_1 (not_1_out, Zwei);
  not not_2 (not_2_out, Vier);
  not not_3 (not_3_out, Eins);
  and _11 (_11_out, Null, Eins, not_1_out, Drei, not_2_out);
  and _29 (_29_out, Null, not_3_out, Zwei, Drei, Vier);
  or or_1 (AutoGelb, _11_out, _29_out);
endmodule

module \Auto_Grün  (
  input  Null,
  input  Eins,
  input  Zwei,
  input  Drei,
  input  Vier,
  output \AutoGrün 
);

  wire auto_gelb_1_autogelb, auto_rot_1_auto_rot, not_1_out, not_2_out;

  Auto_Gelb auto_gelb_1 (
    .Vier(Vier), .Drei(Drei), .Zwei(Zwei), .Eins(Eins), .Null(Null), .AutoGelb(auto_gelb_1_autogelb));
  Auto_Rot auto_rot_1 (.Vier(Vier), .Drei(Drei), .Zwei(Zwei), .Eins(Eins), .Null(Null), .Auto_Rot(auto_rot_1_auto_rot));
  not not_1 (not_1_out, auto_gelb_1_autogelb);
  not not_2 (not_2_out, auto_rot_1_auto_rot);
  and and_1 (\AutoGrün , not_1_out, not_2_out);

  // Notes on the sheet:
  //   GelbPhase
  //   RotPhase
endmodule

module \Fußgänger_Grün  (
  input  Null,
  input  Eins,
  input  Zwei,
  input  Drei,
  input  Vier,
  output \FußGrün 
);

  wire _10_out, _11_out, _30_out, _31_out, auto_rot_1_auto_rot, not_1_out, not_2_out, not_3_out, not_4_out,
       not_5_out, not_6_out, not_7_out, or_1_out;

  not not_1 (not_1_out, Null);
  not not_2 (not_2_out, Zwei);
  not not_3 (not_3_out, Vier);
  not not_4 (not_4_out, Zwei);
  not not_5 (not_5_out, Vier);
  not not_6 (not_6_out, Null);
  Auto_Rot auto_rot_1 (.Vier(Vier), .Drei(Drei), .Zwei(Zwei), .Eins(Eins), .Null(Null), .Auto_Rot(auto_rot_1_auto_rot));
  and _10 (_10_out, not_1_out, Eins, not_2_out, Drei, not_3_out);
  and _11 (_11_out, Null, Eins, not_4_out, Drei, not_5_out);
  and _30 (_30_out, not_6_out, Eins, Zwei, Drei, Vier);
  and _31 (_31_out, Null, Eins, Zwei, Drei, Vier);
  or or_1 (or_1_out, _10_out, _11_out, _30_out, _31_out);
  not not_7 (not_7_out, or_1_out);
  and and_1 (\FußGrün , not_7_out, auto_rot_1_auto_rot);

  // Notes on the sheet:
  //    Autoampel Rot Phase
  //   Beide Ampeln Rot
endmodule

module \Fußgänger_Rot  (
  input  Null,
  input  Eins,
  input  Zwei,
  input  Drei,
  input  Vier,
  output \FußRot 
);

  wire \fußgänger_grün_1_fußgrün , not_1_out;

  \Fußgänger_Grün  \fußgänger_grün_1  (
    .Null(Null), .Eins(Eins), .Zwei(Zwei), .Drei(Drei), .Vier(Vier), .\FußGrün (\fußgänger_grün_1_fußgrün ));
  not not_1 (not_1_out, \fußgänger_grün_1_fußgrün );
  and and_1 (\FußRot , not_1_out, 1'b1);

  // Notes on the sheet:
  //   Fußgänger grün
endmodule

module Freigabe (
  input  \FußgängerRot ,
  input  Knopfdruck,
  input  \Autoampel_Grün ,
  output Freigabe
);

  wire and_1_out, clock_1_out;

  and and_1 (and_1_out, 1'b1, \FußgängerRot , Knopfdruck, \Autoampel_Grün );
  Clock clock_1 (.out(clock_1_out));
  S_R_Flip_Flop s_r_ff_1 (.S(and_1_out), .clk(clock_1_out), .R(Freigabe), .Q(Freigabe));  // open: Qn, preset, reset, en
endmodule
